# Fritzing sketch final_code1 (saved by Fritzing 0.9.3b)
breadboards: 1

parts:
  부품1 = Arduino Uno (Rev3) - ICSP
  J1 = Piezo Speaker
  hc-sr1 = hc-sr04

nets:
  N1: 부품1.D11_PWM/MOSI, J1.pin2
  GND: 부품1.GND, J1.pin1, hc-sr1.GND
  N2: 부품1.D2, hc-sr1.Trig
  N3: 부품1.D4, hc-sr1.Echo
  5V: 부품1.5V, hc-sr1.VCC
