# Fritzing sketch final_code2 (saved by Fritzing 0.9.3b)
breadboards: 1

parts:
  hc-sr1 = hc-sr04
  J1 = Piezo Speaker
  LCD1 = LCD screen
  J2 = Basic Servo
  부품1 = Bluetooth HC-05 Macho  # not connected
  부품2 = Arduino Uno (Rev3) - ICSP

nets:
  VCC: hc-sr1.VCC, LCD1.V0, J2.vcc
  N1: hc-sr1.Trig, 부품2.D2
  N2: hc-sr1.Echo, 부품2.D4
  GND: hc-sr1.GND, J1.pin1, LCD1.VSS, J2.gnd
  N3: J1.pin2, 부품2.D11_PWM/MOSI
  N4: LCD1.R/W, 부품2.A4/SDA
  N5: LCD1.DB0, 부품2.A5/SCL

notes:
  Brown = SDA
  Purple = SCL
